# Fritzing sketch AntiBueeBMP (saved by Fritzing 0.9.3b)
stripboards: 1

parts:
  WeMos_D1_Mini1 = WeMos D1 Mini
  Composant1 = InvenSense MPU6050
  Alimentation_5_0_12V = Camdenboss CTB0158-3 [part_number=CTB0158-3 package=THT]
  12V_caméra = Camdenboss CTB0158-2 [part_number=CTB0158-2 package=THT]
  12V_chauffage = Camdenboss CTB0158-2 [part_number=CTB0158-2 package=THT]
  1wire = female pin header, 2 pins [form="♀ (female)"]
  DHT22 = female pin header, 3 pins [form="♀ (female)"]
  MPU6050 = female pin header, 8 pins [form="♀ (female)"]
  R1 = Resistor [tolerance=±5% resistance=4.7k package="0805 [SMD]"]
  Park = female alternating pin header, 3 pins [form="♀ (female)"]
  J6 = female pin header, 8 pins [form="♀ (female)"]
  J7 = female pin header, 8 pins [form="♀ (female)"]
  BME280 = female pin header, 4 pins [form="♀ (female)"]
  LED = female pin header, 2 pins [form="♀ (female)"]
  Q1 = MOSFET-NCHANNEL [package=to220v]
  R2 = Resistor [tolerance=±5% resistance=1k package="0805 [SMD]"]

nets:
  3V3: WeMos_D1_Mini1.3V3, Composant1.VCC, DHT22.pin1, MPU6050.pin8, R1.Pin_1, J6.pin8, BME280.pin4
  N1: WeMos_D1_Mini1.5V, Alimentation_5_0_12V.pin1, J7.pin8
  N2: WeMos_D1_Mini1.A0, J6.pin2
  N3: WeMos_D1_Mini1.D0, J6.pin3
  N4: WeMos_D1_Mini1.D1, Composant1.SDA, MPU6050.pin5, J7.pin3, BME280.pin1
  N5: WeMos_D1_Mini1.D2, Composant1.SCL, MPU6050.pin6, J7.pin4, BME280.pin2
  N6: WeMos_D1_Mini1.D3, 1wire.pin2, R1.Pin_0, J7.pin5
  N7: WeMos_D1_Mini1.D4, J7.pin6, LED.pin1
  N8: WeMos_D1_Mini1.D5, DHT22.pin3, J6.pin4
  N9: WeMos_D1_Mini1.D6, J6.pin5, Q1.G, R2.Pin_1
  N10: WeMos_D1_Mini1.D7, Park.pin2, J6.pin6
  N11: WeMos_D1_Mini1.D8, Park.pin3, J6.pin7
  N12: WeMos_D1_Mini1.G, Composant1.GND, Alimentation_5_0_12V.pin2, 12V_caméra.pin1, 1wire.pin1, DHT22.pin2, MPU6050.pin7, Park.pin1, J7.pin7, BME280.pin3, LED.pin2, Q1.S, R2.Pin_0
  N13: WeMos_D1_Mini1.RST, J6.pin1
  N14: WeMos_D1_Mini1.RX, J7.pin2
  N15: WeMos_D1_Mini1.TX, J7.pin1
  N16: Composant1.XDA, MPU6050.pin4
  N17: Composant1.XCL, MPU6050.pin3
  N18: Composant1.AD0, MPU6050.pin2
  N19: Composant1.INT, MPU6050.pin1
  N20: Alimentation_5_0_12V.pin3, 12V_caméra.pin2, 12V_chauffage.pin1
  N21: 12V_chauffage.pin2, Q1.D

custom parts:
  WeMos D1 Mini: The D1 mini is a mini wifi board based on ESP-8266EX.
